// Logisim project project.circ as structural Verilog
module main (
  input  f4,
  input  f3,
  input  fo,
  input  f1,
  input  f2,
  input  Reset,
  output [7:0] AT,
  output RM,
  output FS,
  output AM
);

  wire changecomponent_1_cokedispence, coinaccept_1_result, coinaccept_2_result, coinaccept_3_result,
       stockcheck_1_availablestock;
  wire [7:0] adder_1_output_sum;

  coinAccept coinaccept_1 (.coin(fo), .accept(f4), .refuse(f3), .result(coinaccept_1_result));
  coinAccept coinaccept_2 (.coin(f1), .accept(f4), .refuse(f3), .result(coinaccept_2_result));
  coinAccept coinaccept_3 (.coin(f2), .accept(f4), .refuse(f3), .result(coinaccept_3_result));
  stockCheck stockcheck_1 (.clkDecrease(changecomponent_1_cokedispence), .availableStock(stockcheck_1_availablestock));
  coinAcceptSignal coinacceptsignal_1 (.a(f2), .b(f1), .c(fo), .notAllowed(f3), .am(AM));
  not not_1 (FS, stockcheck_1_availablestock);
  adder adder_1 (
    .enable(stockcheck_1_availablestock), .reset(Reset), .f0(coinaccept_1_result), .f1(coinaccept_2_result),
    .f2(coinaccept_3_result), .sold(changecomponent_1_cokedispence), .output_sum(adder_1_output_sum));
  changeComponent changecomponent_1 (
    .sum(adder_1_output_sum), .change(AT), .cokeDispence(changecomponent_1_cokedispence));

  assign RM = Reset;
endmodule

// VHDL entity coinAccept, as the project stores it:
library IEEE;
use IEEE.STD_LOGIC_1164.ALL;

entity coinAccept is
    port(
        coin: in std_logic;
        accept: in std_logic;
        refuse: in std_logic;
        result: out std_logic
    );
end coinAccept;

architecture Behavioral of coinAccept is

begin
    process(coin) begin
    		result <= '0';
        if rising_edge(coin) then
            if accept = '1' and refuse = '0' then
            	result <= '0';
               result <= '1';
            elsif accept = '0' and refuse = '1' then
               result <= '0';
            end if;
        end if;
    end process;
end Behavioral;

// VHDL entity adder, as the project stores it:
library IEEE;
use IEEE.STD_LOGIC_1164.ALL;
use IEEE.NUMERIC_STD.ALL;

entity adder is
    Port (
        enable: in std_logic;
        reset : in std_logic;
        f0: in std_logic;
        f1: in std_logic;
        f2: in std_logic;
        sold: in std_logic;
        output_sum : out std_logic_vector(7 downto 0)
    );
end adder;

architecture Behavioral of adder is
    signal sum_reg : unsigned(7 downto 0) := "00000000";
begin
    process(f0, f1, f2, reset, sold)
    begin
   		if reset = '1' then
            sum_reg <= "00000000";
        elsif sold = '1' then
            sum_reg <= sum_reg - 100;
   		elsif enable = '1' then
            if rising_edge(f0) then
                sum_reg <= sum_reg + 5;
            elsif rising_edge(f1) then
                sum_reg <= sum_reg + 10;
            elsif rising_edge(f2) then
                sum_reg <= sum_reg + 50;
            end if;
        end if;
    end process;
    
    output_sum <= std_logic_vector(sum_reg);
end Behavioral;

// VHDL entity changeComponent, as the project stores it:
LIBRARY ieee;
USE ieee.std_logic_1164.all;
use ieee.numeric_std.all;

ENTITY changeComponent IS
	PORT (
		sum: in std_logic_vector(7 downto 0);
		change: out std_logic_vector(7 downto 0);
		cokeDispence: out std_logic
	);
END changeComponent;

ARCHITECTURE TypeArchitecture OF changeComponent IS
	signal temp : unsigned(7 downto 0);
BEGIN
	process(sum)
	begin
		if unsigned(sum) >= 100 then
			cokeDispence <= '1';
			change <= std_logic_vector(unsigned(sum) - 100);
		else
			cokeDispence <= '0';
			change <= sum;
		end if;
	end process;
END TypeArchitecture;

// VHDL entity coinAcceptSignal, as the project stores it:
library IEEE;
use IEEE.STD_LOGIC_1164.ALL;

entity coinAcceptSignal is
    port(
        a: in std_logic;
        b: in std_logic;
        c: in std_logic;
        notAllowed: in std_logic;
        am: out std_logic
    );
end coinAcceptSignal;

architecture Behavioral of coinAcceptSignal is

begin
process(a, b, c, notAllowed) begin
	if notAllowed = '1' then
		am <= '0';
	else
	    if a'event and a = '1' then
	        am <= '1';
	    elsif a'event and a = '0' then
	        am <= '0';
	    end if;
	    if b'event and b = '1' then
	        am <= '1';
	    elsif b'event and b = '0' then
	        am <= '0';
	    end if;
	    if c'event and c = '1' then
	        am <= '1';
	    elsif c'event and c = '0' then
	        am <= '0';
	    end if;
	end if;
end process;
end Behavioral;

// VHDL entity stockCheck, as the project stores it:
LIBRARY ieee;
USE ieee.std_logic_1164.all;
use ieee.numeric_std.all;

ENTITY stockCheck IS
  PORT (
  	clkDecrease: in std_logic;
  	availableStock: out std_logic
    );
END stockCheck;

ARCHITECTURE TypeArchitecture OF stockCheck IS

signal stock: integer := 10;

BEGIN
	process(clkDecrease) begin


        if rising_edge(clkDecrease) then
                stock <= stock - 1;
        end if;
        if stock > 0 then
            availableStock <= '1';
        else
            availableStock <= '0';
        end if;
	end process;
END TypeArchitecture;
